// Logisim project 4b_NOT_NAND.circ as structural Verilog: 1 circuit, main circuit main
module main (
  input  A2,
  output notA1
);

  nand nand_1 (notA1, A2, A2);

  // Notes on the sheet:
  //   not A usando NAND
endmodule
