// Logisim project 7_demultiplexer.circ as structural Verilog: 1 circuit, main circuit main
module main (
  input  C1,
  input  C0,
  input  E0,
  output S0,
  output S1,
  output S2,
  output S3
);

  wire and_1_out, and_2_out, and_3_out, and_4_out, not_1_out, not_2_out, not_3_out, not_4_out;

  not not_1 (not_1_out, C0);
  not not_2 (not_2_out, C1);
  not not_3 (not_3_out, C1);
  not not_4 (not_4_out, C0);
  and and_1 (and_1_out, not_1_out, not_2_out);
  and and_2 (and_2_out, C0, not_3_out);
  and and_3 (and_3_out, not_4_out, C1);
  and and_4 (and_4_out, C0, C1);
  and and_5 (S0, and_1_out, E0);
  and and_6 (S1, and_2_out, E0);
  and and_7 (S2, and_3_out, E0);
  and and_8 (S3, and_4_out, E0);

  // Notes on the sheet:
  //   Demultiplexer
endmodule
