// Logisim project 10_CarryLeftShifter34.circ as structural Verilog: 1 circuit, main circuit main
module main (
  input  E0,
  input  E1,
  input  E2,
  input  C0,
  output S0,
  output S1,
  output S2,
  output S3
);

  wire and_1_out, and_2_out, and_3_out, and_4_out, not_1_out;

  not not_1 (not_1_out, C0);
  and and_1 (and_1_out, E1, not_1_out);
  and and_2 (and_2_out, E0, C0);
  and and_3 (and_3_out, E2, not_1_out);
  and and_4 (and_4_out, C0, E1);
  and and_5 (S0, E0, not_1_out);
  or or_1 (S1, and_1_out, and_2_out);
  or or_2 (S2, and_3_out, and_4_out);
  and and_6 (S3, C0, E2);

  // Notes on the sheet:
  //   Carry Left Shifter
endmodule
