// Logisim project 11_fullAdder_1bit.circ as structural Verilog: 1 circuit, main circuit main
module main (
  input  A,
  input  B,
  input  C_in,
  output S,
  output C_out
);

  wire and_1_out, and_2_out, xor_1_out, xor_2_out;

  xor xor_1 (xor_1_out, B, A);
  and and_1 (and_1_out, C_in, B);
  and and_2 (and_2_out, A, xor_2_out);
  xor xor_2 (xor_2_out, C_in, B);
  xor xor_3 (S, C_in, xor_1_out);
  or or_1 (C_out, and_1_out, and_2_out);

  // Notes on the sheet:
  //   Full Adder de 1 bit
endmodule
