// Logisim project 13c_inversoAditivoFail.circ as structural Verilog: 1 circuit, main circuit main
module main (
  input  E0,
  input  E1,
  input  E2,
  input  E3,
  output No_Representable,
  output S0,
  output S1,
  output S2,
  output S3
);

  wire negador4bits_1_not_e0, negador4bits_1_not_e1, negador4bits_1_not_e2, negador4bits_1_not_e3, not_1_out,
       not_2_out, not_3_out;

  Negador4bits negador4bits_1 (
    .e0(E0), .e1(E1), .e2(E2), .e3(E3), .not_e0(negador4bits_1_not_e0), .not_e1(negador4bits_1_not_e1),
    .not_e2(negador4bits_1_not_e2), .not_e3(negador4bits_1_not_e3));
  not not_1 (not_1_out, E0);
  not not_2 (not_2_out, E1);
  not not_3 (not_3_out, E2);
  and and_1 (No_Representable, not_1_out, not_2_out, not_3_out, E3);
  adder4bits adder4bits_1 (
    .A0(negador4bits_1_not_e0), .A1(negador4bits_1_not_e1), .A2(negador4bits_1_not_e2),
    .A3(negador4bits_1_not_e3), .B0(1'b1), .B1(1'b0), .B2(1'b0), .B3(1'b0), .S0(S0), .S1(S1), .S2(S2), .S3(S3));  // open: Zero, Negative, Carry, Overflow
endmodule
