// Logisim project 16_RegistroSimple.circ as structural Verilog: 1 circuit, main circuit registro_simple
module registro_simple (
  input  e3,
  input  e2,
  input  e1,
  input  e0,
  input  load,
  input  clk,
  output o0,
  output o1,
  output o2,
  output o3
);

  wire multiplexer_1_out, multiplexer_2_out, multiplexer_3_out, multiplexer_4_out, not_1_out;

  not not_1 (not_1_out, load);
  Multiplexer multiplexer_1 (.in0(e0), .in1(o0), .out(multiplexer_1_out), .sel(not_1_out));
  Multiplexer multiplexer_2 (.in0(e1), .in1(o1), .out(multiplexer_2_out), .sel(not_1_out));
  Multiplexer multiplexer_3 (.in0(e2), .in1(o2), .out(multiplexer_3_out), .sel(not_1_out));
  Multiplexer multiplexer_4 (.in0(e3), .in1(o3), .out(multiplexer_4_out), .sel(not_1_out));
  D_Flip_Flop d_ff_1 (.D(multiplexer_1_out), .clk(clk), .Q(o0));  // open: Qn, preset, reset
  D_Flip_Flop d_ff_2 (.D(multiplexer_2_out), .clk(clk), .Q(o1));  // open: Qn, preset, reset
  D_Flip_Flop d_ff_3 (.D(multiplexer_3_out), .clk(clk), .Q(o2));  // open: Qn, preset, reset
  D_Flip_Flop d_ff_4 (.D(multiplexer_4_out), .clk(clk), .Q(o3));  // open: Qn, preset, reset

  // Notes on the sheet:
  //   Registro Simple
endmodule
