// Logisim project 18_RegistroRestringido.circ as structural Verilog: 1 circuit, main circuit registro_restringido
module registro_restringido (
  input  e3,
  input  e2,
  input  e1,
  input  e0,
  input  clk,
  input  load,
  input  read,
  output o3,
  output o2,
  output o1,
  output o0
);

  wire d_ff_1_q;
  wire [3:0] registro_simple_1_o0;

  D_Flip_Flop d_ff_1 (.D(read), .clk(clk), .Q(d_ff_1_q));  // open: Qn, preset, reset
  registro_simple registro_simple_1 (
    .e3(e3), .e2(e2), .e1(e1), .e0(e0), .load(load), .clk(clk), .o0(registro_simple_1_o0[0]),
    .o1(registro_simple_1_o0[1]), .o2(registro_simple_1_o0[2]), .o3(registro_simple_1_o0[3]));
  Multiplexer #(.width(4)) multiplexer_1 (
    .in0({o3, o2, o1, o0}), .in1(registro_simple_1_o0), .out({o3, o2, o1, o0}), .sel(d_ff_1_q));

  // Notes on the sheet:
  //   Registro de Salida Restringida
endmodule
