// Logisim project 5_AND_NORyNOT.circ as structural Verilog: 1 circuit, main circuit main
module main (
  input  A,
  input  B,
  input  C,
  output ABC
);

  wire nor_1_out, not_1_out, not_2_out, not_3_out, not_4_out;

  not not_1 (not_1_out, A);
  not not_2 (not_2_out, B);
  not not_3 (not_3_out, C);
  nor nor_1 (nor_1_out, not_1_out, not_2_out);
  not not_4 (not_4_out, nor_1_out);
  or or_1 (ABC, not_4_out, not_3_out);

  // Notes on the sheet:
  //   A AND B AND C usando NOR y NOT
endmodule
