// Logisim project 8a_decoder.circ as structural Verilog: 1 circuit, main circuit main
module main (
  input  E0,
  input  E1,
  input  E2,
  input  E3,
  output S1,
  output S0
);

  wire nor_1_out, nor_2_out, xor_1_out, xor_2_out;

  nor nor_1 (nor_1_out, E0, E1);
  xor xor_1 (xor_1_out, E2, E3);
  nor nor_2 (nor_2_out, E0, E2);
  xor xor_2 (xor_2_out, E1, E3);
  and and_1 (S1, nor_1_out, xor_1_out);
  and and_2 (S0, nor_2_out, xor_2_out);

  // Notes on the sheet:
  //   Decoder
endmodule
