// Logisim project 8b_decoder.circ as structural Verilog: 1 circuit, main circuit main
module main (
  input  E0,
  input  E1,
  input  E2,
  input  E3,
  output S1,
  output S0,
  output Valid
);

  wire and_3_out, nor_1_out, nor_2_out, nor_3_out, xor_1_out, xor_2_out, xor_3_out;

  nor nor_1 (nor_1_out, E0, E1);
  xor xor_1 (xor_1_out, E2, E3);
  nor nor_2 (nor_2_out, E0, E2);
  xor xor_2 (xor_2_out, E1, E3);
  nor nor_3 (nor_3_out, E3, E2);
  xor xor_3 (xor_3_out, E1, E0);
  and and_1 (S1, nor_1_out, xor_1_out);
  and and_2 (S0, nor_2_out, xor_2_out);
  and and_3 (and_3_out, nor_3_out, xor_3_out);
  or or_1 (Valid, S1, and_3_out);

  // Notes on the sheet:
  //   Decoder
  //   Valid = 1 si es una entrada valida, 0 si no
endmodule
