// Logisim project 9b_demultiplexer.circ as structural Verilog: 2 circuits, main circuit main
module main (
  input  E0,
  input  C0,
  input  C1,
  output S0,
  output S1,
  output S2,
  output S3
);

  wire decoder9a_1_s0, decoder9a_1_s1, decoder9a_1_s2, decoder9a_1_s3;

  decoder9a decoder9a_1 (
    .E0(C0), .E1(C1), .S0(decoder9a_1_s0), .S1(decoder9a_1_s1), .S2(decoder9a_1_s2), .S3(decoder9a_1_s3));
  and and_1 (S0, decoder9a_1_s0, E0);
  and and_2 (S1, decoder9a_1_s1, E0);
  and and_3 (S2, decoder9a_1_s2, E0);
  and and_4 (S3, decoder9a_1_s3, E0);

  // Notes on the sheet:
  //   Demultiplexer con decoder
endmodule

module decoder9a (
  input  E0,
  input  E1,
  output S0,
  output S1,
  output S2,
  output S3
);

  wire not_1_out, not_2_out;

  not not_1 (not_1_out, E0);
  not not_2 (not_2_out, E1);
  and and_1 (S0, not_1_out, not_2_out);
  and and_2 (S1, E0, not_2_out);
  and and_3 (S2, not_1_out, E1);
  and and_4 (S3, E0, E1);
endmodule
