// Logisim project 12_4bitsAdder.circ as structural Verilog: 2 circuits, main circuit main
module main (
  input  A0,
  input  A1,
  input  A2,
  input  A3,
  input  B0,
  input  B1,
  input  B2,
  input  B3,
  output S0,
  output S1,
  output S2,
  output S3,
  output Zero,
  output Negative,
  output Carry,
  output Overflow
);

  wire A0plusB0_c_out, A1plusB1_c_out, A2plusB2_c_out, not_1_out, not_2_out, not_3_out, not_4_out;

  adder1bit A0plusB0 (.A(A0), .B(B0), .S(S0), .C_out(A0plusB0_c_out));  // open: C_in
  adder1bit A1plusB1 (.A(A1), .B(B1), .C_in(A0plusB0_c_out), .S(S1), .C_out(A1plusB1_c_out));
  adder1bit A2plusB2 (.A(A2), .B(B2), .C_in(A1plusB1_c_out), .S(S2), .C_out(A2plusB2_c_out));
  adder1bit A3plusB3 (.A(A3), .B(B3), .C_in(A2plusB2_c_out), .S(Negative), .C_out(Carry));
  not not_1 (not_1_out, Negative);
  not not_2 (not_2_out, S2);
  not not_3 (not_3_out, S1);
  and and_1 (Zero, not_1_out, not_2_out, not_3_out, not_4_out);
  xor xor_1 (Overflow, A2plusB2_c_out, Carry);
  not not_4 (not_4_out, S0);

  assign S3 = Negative;

  // Notes on the sheet:
  //   Full Adder de 4 bits
endmodule

module adder1bit (
  input  A,
  input  B,
  input  C_in,
  output S,
  output C_out
);

  wire and_1_out, and_2_out, xor_1_out, xor_2_out;

  xor xor_1 (xor_1_out, C_in, B);
  xor xor_2 (xor_2_out, B, A);
  and and_1 (and_1_out, C_in, B);
  and and_2 (and_2_out, A, xor_1_out);
  xor xor_3 (S, C_in, xor_2_out);
  or or_1 (C_out, and_1_out, and_2_out);
endmodule
