// Logisim project 13_inversoAditivo.circ as structural Verilog: 4 circuits, main circuit inversoAditivoComplem2
module inversoAditivoComplem2 (
  input  E0,
  input  E1,
  input  E2,
  input  E3,
  output S0,
  output S1,
  output S2,
  output S3
);

  wire negador4bits_1_not_e0, negador4bits_1_not_e1, negador4bits_1_not_e2, negador4bits_1_not_e3;

  Negador4bits negador4bits_1 (
    .e0(E0), .e1(E1), .e2(E2), .e3(E3), .not_e0(negador4bits_1_not_e0), .not_e1(negador4bits_1_not_e1),
    .not_e2(negador4bits_1_not_e2), .not_e3(negador4bits_1_not_e3));
  adder4bits adder4bits_1 (
    .A0(negador4bits_1_not_e0), .A1(negador4bits_1_not_e1), .A2(negador4bits_1_not_e2),
    .A3(negador4bits_1_not_e3), .B0(1'b1), .B1(1'b0), .B2(1'b0), .B3(1'b0), .S0(S0), .S1(S1), .S2(S2), .S3(S3));  // open: Zero, Negative, Carry, Overflow

  // Notes on the sheet:
  //   Inverso Aditivo en complemento a 2
endmodule

module Negador4bits (
  input  e0,
  input  e1,
  input  e2,
  input  e3,
  output not_e0,
  output not_e1,
  output not_e2,
  output not_e3
);

  not not_1 (not_e0, e0);
  not not_2 (not_e1, e1);
  not not_3 (not_e2, e2);
  not not_4 (not_e3, e3);
endmodule

module adder1bit (
  input  A,
  input  B,
  input  C_in,
  output S,
  output C_out
);

  wire and_1_out, and_2_out, xor_1_out, xor_2_out;

  xor xor_1 (xor_1_out, C_in, B);
  xor xor_2 (xor_2_out, B, A);
  and and_1 (and_1_out, C_in, B);
  and and_2 (and_2_out, A, xor_1_out);
  xor xor_3 (S, C_in, xor_2_out);
  or or_1 (C_out, and_1_out, and_2_out);
endmodule

module adder4bits (
  input  A0,
  input  A1,
  input  A2,
  input  A3,
  input  B0,
  input  B1,
  input  B2,
  input  B3,
  output S0,
  output S1,
  output S2,
  output S3,
  output Zero,
  output Negative,
  output Carry,
  output Overflow
);

  wire A0plusB0_c_out, A1plusB1_c_out, A2plusB2_c_out, not_1_out, not_2_out, not_3_out, not_4_out;

  adder1bit A0plusB0 (.A(A0), .B(B0), .S(S0), .C_out(A0plusB0_c_out));  // open: C_in
  adder1bit A1plusB1 (.A(A1), .B(B1), .C_in(A0plusB0_c_out), .S(S1), .C_out(A1plusB1_c_out));
  adder1bit A2plusB2 (.A(A2), .B(B2), .C_in(A1plusB1_c_out), .S(S2), .C_out(A2plusB2_c_out));
  adder1bit A3plusB3 (.A(A3), .B(B3), .C_in(A2plusB2_c_out), .S(Negative), .C_out(Carry));
  not not_1 (not_1_out, Negative);
  not not_2 (not_2_out, S2);
  not not_3 (not_3_out, S1);
  and and_1 (Zero, not_1_out, not_2_out, not_3_out, not_4_out);
  xor xor_1 (Overflow, A2plusB2_c_out, Carry);
  not not_4 (not_4_out, S0);

  assign S3 = Negative;

  // Notes on the sheet:
  //   Full Adder de 4 bits
endmodule
