// Logisim project 17_ExtensorDeSigno.circ as structural Verilog: 1 circuit, main circuit main
module main (
  input  e3,
  input  e2,
  input  e1,
  input  e0,
  input  load,
  input  ext,
  output o0,
  output o1,
  output o2,
  output o3
);

  wire clk_out, d_ff_1_q, d_ff_2_q, d_ff_3_q, d_ff_4_q, multiplexer_1_out, multiplexer_2_out,
       multiplexer_3_out, multiplexer_4_out, not_1_out;

  not not_1 (not_1_out, load);
  Multiplexer multiplexer_1 (.in0(e0), .in1(d_ff_1_q), .out(multiplexer_1_out), .sel(not_1_out));
  Multiplexer multiplexer_2 (.in0(e1), .in1(d_ff_2_q), .out(multiplexer_2_out), .sel(not_1_out));
  Multiplexer multiplexer_3 (.in0(e2), .in1(d_ff_3_q), .out(multiplexer_3_out), .sel(not_1_out));
  Multiplexer multiplexer_4 (.in0(e3), .in1(d_ff_4_q), .out(multiplexer_4_out), .sel(not_1_out));
  Clock clk (.out(clk_out));
  D_Flip_Flop d_ff_1 (.D(multiplexer_1_out), .clk(clk_out), .Q(d_ff_1_q));  // open: Qn, preset, reset
  D_Flip_Flop d_ff_2 (.D(multiplexer_2_out), .clk(clk_out), .Q(d_ff_2_q));  // open: Qn, preset, reset
  D_Flip_Flop d_ff_3 (.D(multiplexer_3_out), .clk(clk_out), .Q(d_ff_3_q));  // open: Qn, preset, reset
  D_Flip_Flop d_ff_4 (.D(multiplexer_4_out), .clk(clk_out), .Q(d_ff_4_q));  // open: Qn, preset, reset
  Multiplexer multiplexer_5 (.in0(d_ff_1_q), .in1(e1), .out(o0), .sel(ext));
  Multiplexer multiplexer_6 (.in0(d_ff_2_q), .in1(e1), .out(o1), .sel(ext));
  Multiplexer multiplexer_7 (.in0(d_ff_3_q), .in1(e1), .out(o2), .sel(ext));
  Multiplexer multiplexer_8 (.in0(d_ff_4_q), .in1(e0), .out(o3), .sel(ext));

  // Notes on the sheet:
  //   Extensor de Signo
endmodule
