// Logisim project 19_RegistroBidirecional.circ as structural Verilog: 1 circuit, main circuit registro_bidireccional
module registro_bidireccional (
  input  [3:0] di,
  input  clk,
  input  load,
  input  read
);

  registro_restringido registro_restringido_1 (
    .e3(di[3]), .e2(di[2]), .e1(di[1]), .e0(di[0]), .clk(clk), .load(load), .read(read), .o3(di[3]),
    .o2(di[2]), .o1(di[1]), .o0(di[0]));
endmodule
