// Logisim project 4a_AND_NAND.circ as structural Verilog: 1 circuit, main circuit main
module main (
  input  A,
  input  B,
  output AB
);

  wire nand_1_out;

  nand nand_1 (nand_1_out, A, B);
  nand nand_2 (AB, nand_1_out, nand_1_out);

  // Notes on the sheet:
  //   AND usando dos NAND
endmodule
