// Logisim project 9a_decoder.circ as structural Verilog: 1 circuit, main circuit main
module main (
  input  E0,
  input  E1,
  output S0,
  output S1,
  output S2,
  output S3
);

  wire not_1_out, not_2_out;

  not not_1 (not_1_out, E0);
  not not_2 (not_2_out, E1);
  and and_1 (S0, not_1_out, not_2_out);
  and and_2 (S1, E0, not_2_out);
  and and_3 (S2, not_1_out, E1);
  and and_4 (S3, E0, E1);

  // Notes on the sheet:
  //   Decodificador
endmodule
