// Logisim project TallerLogica-Combinatorios.circ as structural Verilog: 10 circuits, main circuit verificador
module sumador_simple (
  input  A,
  input  B,
  output S,
  output Cout
);

  xor xor_1 (S, A, B);
  and and_1 (Cout, B, A);
endmodule

module sumador_completo (
  input  A,
  input  B,
  input  Cin,
  output S,
  output Cout
);

  wire and_1_out, and_2_out, xor_1_out, xor_2_out;

  xor xor_1 (xor_1_out, A, B);
  and and_1 (and_1_out, B, Cin);
  xor xor_2 (xor_2_out, Cin, B);
  xor xor_3 (S, xor_1_out, Cin);
  and and_2 (and_2_out, A, xor_2_out);
  or or_1 (Cout, and_1_out, and_2_out);
endmodule

module sumador_4 (
  input  [3:0] A,
  input  [3:0] B,
  input  Cin,
  output [3:0] S,
  output Cout
);

  wire sumador_completo_1_cout, sumador_completo_2_cout, sumador_completo_3_cout;

  sumador_completo sumador_completo_1 (.A(A[0]), .B(B[0]), .Cin(Cin), .S(S[0]), .Cout(sumador_completo_1_cout));
  sumador_completo sumador_completo_2 (
    .A(A[1]), .B(B[1]), .Cin(sumador_completo_1_cout), .S(S[1]), .Cout(sumador_completo_2_cout));
  sumador_completo sumador_completo_3 (
    .A(A[2]), .B(B[2]), .Cin(sumador_completo_2_cout), .S(S[2]), .Cout(sumador_completo_3_cout));
  sumador_completo sumador_completo_4 (.A(A[3]), .B(B[3]), .Cin(sumador_completo_3_cout), .S(S[3]), .Cout(Cout));
  Hex_Digit_Display hex_digit_display_1 (.value(S));  // open: dp
endmodule

module comparador_cero (
  input  [3:0] A,
  output Z
);

  wire [3:0] not_1_out;

  assign not_1_out = ~A;  // NOT_Gate not_1, 4 bits wide
  and and_1 (Z, not_1_out[0], not_1_out[1], not_1_out[2], not_1_out[3]);
endmodule

module sumador_flags (
  input  [3:0] A,
  input  [3:0] B,
  input  Cin,
  output [3:0] S,
  output Z,
  output C,
  output N,
  output V
);

  wire and_1_out, and_2_out, not_1_out, not_2_out, not_3_out, sumador_completo_1_cout,
       sumador_completo_2_cout, sumador_completo_3_cout;

  sumador_completo sumador_completo_1 (.A(A[0]), .B(B[0]), .Cin(Cin), .S(S[0]), .Cout(sumador_completo_1_cout));
  sumador_completo sumador_completo_2 (
    .A(A[1]), .B(B[1]), .Cin(sumador_completo_1_cout), .S(S[1]), .Cout(sumador_completo_2_cout));
  sumador_completo sumador_completo_3 (
    .A(A[2]), .B(B[2]), .Cin(sumador_completo_2_cout), .S(S[2]), .Cout(sumador_completo_3_cout));
  sumador_completo sumador_completo_4 (.A(A[3]), .B(B[3]), .Cin(sumador_completo_3_cout), .S(N), .Cout(C));
  Hex_Digit_Display hex_digit_display_1 (.value({N, S[2:0]}));  // open: dp
  not not_1 (not_1_out, N);
  not not_2 (not_2_out, A[3]);
  not not_3 (not_3_out, B[3]);
  and and_1 (and_1_out, A[3], B[3], not_1_out);
  and and_2 (and_2_out, not_2_out, not_3_out, N);
  comparador_cero comparador_cero_1 (.Z(Z));  // open: A
  or or_1 (V, and_1_out, and_2_out);

  assign S[3] = N;
endmodule

module incrementador_4 (
  input  [3:0] A,
  output [3:0] S
);

  Hex_Digit_Display hex_digit_display_1 (.value(S));  // open: dp
  sumador_4 sumador_4_1 (.A(A), .B(4'b0001), .Cin(1'b0), .S(S));  // open: Cout
endmodule

module inversor_4 (
  input  [3:0] A,
  input  INV,
  output [3:0] S
);

  wire [3:0] incrementador_4_1_s, not_1_out;

  assign not_1_out = ~A;  // NOT_Gate not_1, 4 bits wide
  incrementador_4 incrementador_4_1 (.A(not_1_out), .S(incrementador_4_1_s));
  Multiplexer #(.width(4)) multiplexer_1 (.in0(A), .in1(incrementador_4_1_s), .out(S), .sel(INV));
  Hex_Digit_Display hex_digit_display_1 (.value(S));  // open: dp
endmodule

module ALU (
  input  [3:0] A,
  input  [3:0] B,
  input  [1:0] OP,
  output N,
  output Z,
  output V,
  output C,
  output [3:0] S
);

  wire aluresta_1_borrow, aluresta_1_v, sumador_flags_1_c, sumador_flags_1_v;
  wire [3:0] aluresta_1_s, and_1_out, or_1_out, sumador_flags_1_s;

  assign or_1_out = A | B;  // OR_Gate or_1, 4 bits wide
  assign and_1_out = A & B;  // AND_Gate and_1, 4 bits wide
  sumador_flags sumador_flags_1 (
    .A(A), .B(B), .S(sumador_flags_1_s), .C(sumador_flags_1_c), .V(sumador_flags_1_v));  // open: Cin, Z, N
  AluResta aluresta_1 (.A(A), .B(B), .S(aluresta_1_s), .Borrow(aluresta_1_borrow), .V(aluresta_1_v));
  Multiplexer #(.select(2), .width(4)) multiplexer_1 (
    .in0(sumador_flags_1_s), .in1(aluresta_1_s), .in2(or_1_out), .in3(and_1_out), .out({N, S[2:0]}), .sel(OP));
  Multiplexer #(.select(2)) multiplexer_2 (
    .in0(sumador_flags_1_v), .in1(aluresta_1_v), .in2(1'b0), .in3(1'b0), .out(V), .sel(OP));
  Hex_Digit_Display hex_digit_display_1 (.value({N, S[2:0]}));  // open: dp
  comparador_cero comparador_cero_1 (.A({N, S[2:0]}), .Z(Z));
  Multiplexer #(.select(2)) multiplexer_3 (
    .in0(sumador_flags_1_c), .in1(aluresta_1_borrow), .in2(1'b0), .in3(1'b0), .out(C), .sel(OP));

  assign S[3] = N;
endmodule

module verificador (
  output [3:0] out_1,
  output [3:0] out_2,
  output [1:0] out_3,
  output halt,
  output N,
  output Z,
  output V,
  output C,
  output [3:0] res
);

  wire clock_1_out;

  Clock clock_1 (.out(clock_1_out));
  Counter #(.max('h3ff), .width(10)) counter_1 (
    .clk(clock_1_out), .carry(halt), .Q({out_3, out_2, out_1}));  // open: clr, load, up, count, D
  ALU alu_1 (.A(out_1), .B(out_2), .OP(out_3), .N(N), .Z(Z), .V(V), .C(C), .S(res));
endmodule

module AluResta (
  input  [3:0] A,
  input  [3:0] B,
  output [3:0] S,
  output Borrow,
  output V
);

  wire and_1_out, comparador_cero_1_z, not_1_out, not_2_out, not_3_out, not_4_out, not_5_out, not_6_out,
       sumador_flags_1_c, sumador_flags_1_v;
  wire [3:0] inversor_4_1_s;

  inversor_4 inversor_4_1 (.A(B), .INV(1'b1), .S(inversor_4_1_s));
  not not_1 (not_1_out, B[0]);
  not not_2 (not_2_out, B[1]);
  not not_3 (not_3_out, B[2]);
  and and_1 (and_1_out, not_1_out, not_2_out, not_3_out, B[3]);
  sumador_flags sumador_flags_1 (
    .A(A), .B(inversor_4_1_s), .Cin(1'b0), .S(S), .C(sumador_flags_1_c), .V(sumador_flags_1_v));  // open: Z, N
  not not_4 (not_4_out, sumador_flags_1_v);
  Multiplexer multiplexer_1 (.in0(sumador_flags_1_v), .in1(not_4_out), .out(V), .sel(and_1_out));
  comparador_cero comparador_cero_1 (.A(inversor_4_1_s), .Z(comparador_cero_1_z));
  not not_5 (not_5_out, comparador_cero_1_z);
  not not_6 (not_6_out, sumador_flags_1_c);
  and and_2 (Borrow, not_5_out, not_6_out);
endmodule
